// Logisim project adderCircuit.circ as structural Verilog: 1 circuit, main circuit main
module main (
  input  operands,
  input  in_2,
  input  in_3,
  input  in_4,
  input  in_5,
  input  in_6,
  input  in_7,
  input  in_8,
  output remainder,
  output sum,
  output out_11,
  output out_12,
  output out_13
);

  wire and_1_out, and_2_out, and_3_out, and_4_out, and_5_out, and_6_out, and_7_out, or_1_out, or_2_out,
       xor_1_out, xor_2_out, xor_3_out;

  and and_1 (and_1_out, in_2, in_6);
  and and_2 (and_2_out, operands, in_5);
  and and_3 (and_3_out, in_4, in_8);
  xor xor_1 (xor_1_out, in_3, in_7);
  and and_4 (and_4_out, in_3, in_7);
  xor xor_2 (xor_2_out, in_2, in_6);
  xor xor_3 (xor_3_out, operands, in_5);
  xor xor_4 (out_13, in_4, in_8);
  xor xor_5 (out_12, xor_1_out, and_3_out);
  and and_5 (and_5_out, xor_1_out, and_3_out);
  xor xor_6 (out_11, xor_2_out, or_1_out);
  and and_6 (and_6_out, xor_2_out, or_1_out);
  xor xor_7 (sum, xor_3_out, or_2_out);
  and and_7 (and_7_out, xor_3_out, or_2_out);
  or or_1 (or_1_out, and_5_out, and_4_out);
  or or_2 (or_2_out, and_6_out, and_1_out);
  or or_3 (remainder, and_7_out, and_2_out);

  // Notes on the sheet:
  //   h
  //   g
  //   f
  //   e
endmodule
